# Fritzing sketch Dome_Schematic (saved by Fritzing 0.8.7b)

parts:
  Part2 = Arduino Mega 2560 (Rev3)
  M1 = DC Motor
  LED1 = LED - 5mm [color="Blue (470nm)" package="5 mm [THT]"]
  LED2 = LED - 5mm [color="Red (633nm)" package="5 mm [THT]"]
  LED3 = LED - 5mm [color="White (8000K)" package="5 mm [THT]"]
  LED4 = LED - 5mm [color="White (8000K)" package="5 mm [THT]"]
  LED5 = LED - 5mm [color="Red (633nm)" package="5 mm [THT]"]
  Q2 = Basic FET N-Channel [package="TO220 [THT]"]
  R2 = Resistor [tolerance=±5% resistance=47k package=THT]
  R3 = Resistor [tolerance=±5% resistance=1.2 package=THT]
  R4 = Resistor [tolerance=±5% resistance=0.1 package=THT]
  R5 = Resistor [tolerance=±5% resistance=1.2 package=THT]
  Q3 = Basic FET N-Channel [package="TO220 [THT]"]
  R6 = Resistor [tolerance=±5% resistance=47k package=THT]
  Q4 = Basic FET N-Channel [package="TO220 [THT]"]
  R7 = Resistor [tolerance=±5% resistance=47k package=THT]
  Q7 = Basic FET N-Channel [package="TO220 [THT]"]
  R10 = Resistor [tolerance=±5% resistance=47k package=THT]
  R12 = Resistor [tolerance=±5% resistance=1.2 package=THT]
  Ethernet_Shield = Arduino Ethernet Shield (Rev3)
  Tank_level = VARISTOR [package=0603-res]
  Soil_Moisture = VARISTOR [package=0603-res]
  Q8 = NPN-Transistor [package="TO92 [THT]"]
  R13 = Resistor [tolerance=±5% resistance=330 package=THT]
  K1 = Relay [part_number=FRS1B-S package=THT]

nets:
  N1: Part2.A0, Part2.5V, Tank_level.1, Soil_Moisture.1
  N2: Part2.GND, Q2.source, R2.Pin_1, Q3.source, R6.Pin_1, Q4.source, Q7.source, Tank_level.2, Soil_Moisture.2, Q8.E, K1.A
  N3: Part2.D13_PWM, Ethernet_Shield.SPI/D13
  N4: Part2.D12_PWM, Ethernet_Shield.SPI/D12
  N5: Part2.D11_PWM, Ethernet_Shield.PWM_D11
  N6: Part2.D10_PWM, Ethernet_Shield.ETH_CS
  N7: Part2.D9_PWM, Q4.gate, R7.Pin_0
  N8: Part2.D8_PWM, Q7.gate
  N9: Part2.D4_PWM, Ethernet_Shield.SDCS
  N10: Part2.D6_PWM, Q3.gate, R6.Pin_0
  N11: Part2.D7_PWM, Q2.gate, R2.Pin_0
  N12: Part2.D22, R13.Pin_0
  5V: M1.pin_1, LED1.anode, LED2.anode, LED3.anode, LED4.anode, LED5.anode, K1.COIL2
  N13: M1.pin_2, K1.B
  N14: LED1.cathode, R3.Pin_0
  N15: LED2.cathode, R5.Pin_0
  N16: LED3.cathode, LED4.cathode, R4.Pin_0
  N17: LED5.cathode, R12.Pin_0
  N18: Q2.drain, R3.Pin_1
  N19: R4.Pin_1, Q3.drain
  N20: R5.Pin_1, Q4.drain
  N21: R7.Pin_1, R10.Pin_1
  N22: Q7.drain, R12.Pin_1
  N23: Q8.B, R13.Pin_1
  N24: Q8.C, K1.COIL1, K1.C1, K1.C2
